// Logisim project S1-T12.circ as structural Verilog: 20 circuits, main circuit main
module main (
  input  [3:0] City_Population_Rate,
  input  [2:0] Town_Population_Rate,
  input  Population_Adder,
  input  Population_Subtractor,
  input  Population_Adder_2,
  input  Population_Subtractor_2,
  input  [5:0] Water_Collection_Rate,
  input  Pump_Switch,
  output _100,
  output _75,
  output _100_2,
  output _50,
  output _60,
  output _25,
  output _30,
  output ALARM____TOWN_UNDERFLOW,
  output ALARM____CITY_UNDERFLOW,
  output _100_3,
  output _75_2,
  output Water_Reservoir_Overflow,
  output _50_2,
  output _25_2,
  output _10
);

  wire and_4_out, and_8_out, and_16_out, and_20_out, n3_bit_adder_1_overflow,
       n3_bit_subtractor_1_overflow__1___if_bigger___smaller, n4_bit_adder_1_overflow,
       n4_bit_subtractor_1_overflow__1___if_bigger___smaller, n6_bit_adder_1_overflow,
       n6_bit_subtractor_2_overflow__1___if_bigger___smaller, not_5_out, or_2_out, or_3_out, or_5_out,
       Reset_out, xor_1_out, xor_2_out;
  wire [1:0] and_10_out;
  wire [2:0] and_13_out, and_14_out, and_17_out, and_18_out, n3_bit_adder_1_sum,
       n3_bit_subtractor_1_difference, or_4_out;
  wire [2:2] and_15_out, and_19_out, not_6_out, not_7_out;
  wire [3:0] and_1_out, and_2_out, and_5_out, and_6_out, City_Water_Demand__4_bit_stored_output,
       n3_4_convertor_4_bit_1_input_3_4, n4_bit_adder_1_sum, n4_bit_subtractor_1_difference, or_1_out;
  wire [3:3] and_3_out, and_7_out, not_1_out, not_2_out;
  wire [4:0] Treatment_of_Sewage_input_3_4;
  wire [5:0] and_9_out, and_11_out, multiplexer_1_out, n6_bit_adder_1_sum, n6_bit_subtractor_2_difference,
       n6_bit_subtractor_3_difference, Sewage_Collection_Centre_sum, Water_Adder_to_Reservoir_sum,
       Water_Reservoir_Storage__6_bit_stored_output;
  wire [5:3] n3_4_convertor_3_bit_1_input_3_4, Town_Water_Demand__3_bit_stored_output;
  wire [5:5] not_3_out, not_4_out;

  assign and_1_out = and_2_out & {4{and_3_out[3]}};  // AND_Gate and_1, 4 bits wide
  assign and_2_out = n4_bit_adder_1_sum & {4{not_1_out[3]}};  // AND_Gate and_2, 4 bits wide
  not not_1 (not_1_out[3], n4_bit_adder_1_overflow);
  _4_bit_Adder u_4_bit_adder_1 (
    .Input1(City_Water_Demand__4_bit_stored_output), .Input2(City_Population_Rate), .Sum(n4_bit_adder_1_sum),
    .Overflow(n4_bit_adder_1_overflow));
  assign or_1_out = and_1_out | and_5_out;  // OR_Gate or_1, 4 bits wide
  and and_3 (and_3_out[3], not_1_out[3], and_4_out);
  and and_4 (and_4_out, Population_Adder, xor_1_out);
  Display___4_bit City_Population (
    .Input(City_Water_Demand__4_bit_stored_output), ._100(_100), ._75(_75), ._50(_50), ._25(_25));
  _4_bit_FlipFlop_D City_Water_Demand (
    ._4_Bit_Input(or_1_out), .Load__1_updates_the_memory(or_2_out),
    ._4_Bit_Stored_Output(City_Water_Demand__4_bit_stored_output), .Reset(Reset_out));
  or or_2 (or_2_out, and_3_out[3], and_7_out[3]);
  assign and_5_out = and_6_out & {4{and_7_out[3]}};  // AND_Gate and_5, 4 bits wide
  assign and_6_out = n4_bit_subtractor_1_difference & {4{not_2_out[3]}};  // AND_Gate and_6, 4 bits wide
  not not_2 (not_2_out[3], n4_bit_subtractor_1_overflow__1___if_bigger___smaller);
  xor xor_1 (xor_1_out, Population_Adder, Population_Subtractor);
  and and_7 (and_7_out[3], not_2_out[3], and_8_out);
  and and_8 (and_8_out, xor_1_out, Population_Subtractor);
  _4_bit_Subtractor u_4_bit_subtractor_1 (
    .Bigger_Number(City_Water_Demand__4_bit_stored_output), .Smaller_Number(City_Population_Rate),
    .Difference(n4_bit_subtractor_1_difference),
    .Overflow__1___if_Bigger___Smaller(n4_bit_subtractor_1_overflow__1___if_bigger___smaller));
  _3_4_convertor___4_bit u_3_4_convertor_4_bit_1 (
    .Input(City_Water_Demand__4_bit_stored_output), .Input_3_4(n3_4_convertor_4_bit_1_input_3_4));
  _6_bit_subtractor u_6_bit_subtractor_1 (
    .Bigger_Number(Water_Reservoir_Storage__6_bit_stored_output),
    .Smaller_Number({2'b00, City_Water_Demand__4_bit_stored_output}),
    .Overflow__1___if_Bigger___Smaller(ALARM____CITY_UNDERFLOW));  // open: Difference
  Button Reset (.out(Reset_out));
  assign and_9_out = n6_bit_subtractor_2_difference & {6{not_3_out[5]}};  // AND_Gate and_9, 6 bits wide
  not not_3 (not_3_out[5], n6_bit_subtractor_2_overflow__1___if_bigger___smaller);
  _6_bit_subtractor u_6_bit_subtractor_2 (
    .Bigger_Number(Water_Reservoir_Storage__6_bit_stored_output),
    .Smaller_Number(n6_bit_subtractor_3_difference), .Difference(n6_bit_subtractor_2_difference),
    .Overflow__1___if_Bigger___Smaller(n6_bit_subtractor_2_overflow__1___if_bigger___smaller));
  and and_10 (and_10_out[0], not_3_out[5], not_5_out);
  Display___6_bit Water_Reservoir_Level (
    .Input(Water_Reservoir_Storage__6_bit_stored_output), ._100(_100_3), ._75(_75_2), ._50(_50_2),
    ._25(_25_2), ._10(_10));
  _6_Bit_FlipFlop_D Water_Reservoir_Storage (
    ._6_Bit_Input(multiplexer_1_out), ._6_Bit_Stored_Output(Water_Reservoir_Storage__6_bit_stored_output),
    .Load__1_updates_the_memory(1'b1), .Reset(Reset_out));
  Multiplexer #(.select(2), .width(6)) multiplexer_1 (
    .in0(Water_Reservoir_Storage__6_bit_stored_output), .in1(and_9_out), .in2(and_11_out),
    .in3(n6_bit_adder_1_sum), .out(multiplexer_1_out), .sel(and_10_out), .en(1'b1));
  _6_bit_Adder u_6_bit_adder_1 (
    .Input1(and_9_out), .Input2(and_11_out), .Sum(n6_bit_adder_1_sum), .Overflow(n6_bit_adder_1_overflow));
  _6_bit_Adder Water_Adder_to_Reservoir (
    .Input1(Water_Reservoir_Storage__6_bit_stored_output), .Input2(Water_Collection_Rate),
    .Sum(Water_Adder_to_Reservoir_sum), .Overflow(Water_Reservoir_Overflow));
  _6_bit_Adder Sewage_Collection_Centre (
    .Input1({2'b00, n3_4_convertor_4_bit_1_input_3_4}), .Input2({n3_4_convertor_3_bit_1_input_3_4, 3'b000}),
    .Sum(Sewage_Collection_Centre_sum));  // open: Overflow
  _6_bit_subtractor u_6_bit_subtractor_3 (
    .Bigger_Number({1'b0, Treatment_of_Sewage_input_3_4}), .Smaller_Number(Sewage_Collection_Centre_sum),
    .Difference(n6_bit_subtractor_3_difference));  // open: Overflow__1___if_Bigger___Smaller
  assign and_11_out = Water_Adder_to_Reservoir_sum & {6{not_4_out[5]}};  // AND_Gate and_11, 6 bits wide
  not not_4 (not_4_out[5], Water_Reservoir_Overflow);
  _3_4_convertor___5_bit Treatment_of_Sewage (
    .Input(Sewage_Collection_Centre_sum[4:0]), .Input_3_4(Treatment_of_Sewage_input_3_4));
  and and_12 (and_10_out[1], not_4_out[5], Pump_Switch);
  not not_5 (not_5_out, or_3_out);
  or or_3 (or_3_out, ALARM____CITY_UNDERFLOW, ALARM____TOWN_UNDERFLOW);
  _6_bit_subtractor u_6_bit_subtractor_4 (
    .Bigger_Number(Water_Reservoir_Storage__6_bit_stored_output),
    .Smaller_Number({Town_Water_Demand__3_bit_stored_output, 3'b000}),
    .Overflow__1___if_Bigger___Smaller(ALARM____TOWN_UNDERFLOW));  // open: Difference
  _3_4_convertor___3_bit u_3_4_convertor_3_bit_1 (
    .Input(Town_Water_Demand__3_bit_stored_output), .Input_3_4(n3_4_convertor_3_bit_1_input_3_4));
  _3_bit_Adder u_3_bit_adder_1 (
    .Input1(Town_Water_Demand__3_bit_stored_output), .Input2(Town_Population_Rate), .Sum(n3_bit_adder_1_sum),
    .Overflow(n3_bit_adder_1_overflow));
  assign and_13_out = and_14_out & {3{and_15_out[2]}};  // AND_Gate and_13, 3 bits wide
  assign and_14_out = n3_bit_adder_1_sum & {3{not_6_out[2]}};  // AND_Gate and_14, 3 bits wide
  not not_6 (not_6_out[2], n3_bit_adder_1_overflow);
  _3_bit_FlipFlop__D Town_Water_Demand (
    ._3_Bit_Input(or_4_out), .Load__1_updates_the_memory(or_5_out),
    ._3_Bit_Stored_Output(Town_Water_Demand__3_bit_stored_output), .Reset(Reset_out));
  assign or_4_out = and_13_out | and_17_out;  // OR_Gate or_4, 3 bits wide
  and and_15 (and_15_out[2], not_6_out[2], and_16_out);
  and and_16 (and_16_out, Population_Adder_2, xor_2_out);
  Display___3_bit Town_Population (.Input(Town_Water_Demand__3_bit_stored_output), ._100(_100_2), ._60(_60), ._30(_30));
  assign and_17_out = and_18_out & {3{and_19_out[2]}};  // AND_Gate and_17, 3 bits wide
  assign and_18_out = n3_bit_subtractor_1_difference & {3{not_7_out[2]}};  // AND_Gate and_18, 3 bits wide
  xor xor_2 (xor_2_out, Population_Adder_2, Population_Subtractor_2);
  or or_5 (or_5_out, and_15_out[2], and_19_out[2]);
  not not_7 (not_7_out[2], n3_bit_subtractor_1_overflow__1___if_bigger___smaller);
  and and_19 (and_19_out[2], not_7_out[2], and_20_out);
  _3_bit_Subtractor u_3_bit_subtractor_1 (
    .Bigger_Number(Town_Water_Demand__3_bit_stored_output), .Smaller_Number(Town_Population_Rate),
    .Difference(n3_bit_subtractor_1_difference),
    .Overflow__1___if_Bigger___Smaller(n3_bit_subtractor_1_overflow__1___if_bigger___smaller));
  and and_20 (and_20_out, xor_2_out, Population_Subtractor_2);

  // Notes on the sheet:
  //   THE CITY
  //   SEWAGE BOARD & WATER MANAGEMENT
  //   OVERALL CIRCUIT
  //   WATER RESERVOIR
  //   TEAM MEMBERS:
  //   3. Jeferson || 231CS131
  //   INSTRUCTIONS:
  //   NOTE:
  //   1. Vamshi Chethan A M || 231CS162
  //   2. Maley Srijan || 231CS133
  //   1. FIrstly, Set the Population Rate for City & Down using the 4-bit & 3-bit input respectively
  //   2. Toggle the Population Adder Switch to Increase the Given Rate of Population for a day (10-ticks)
  //   8. To Reset, Revert Every Binary Input to '0's and press the Reset Button to Reset the Circuit.
  //   4. You will notice the water decrementing slowly with time due to consumption from the city & town and about 9/16th of it being recycled
  //   3. Set the "Water Collection Rate" using the 6-bit input, and use the "Pump Switch" to pump the input water to the water reservoir every half-day (5-ticks)
  //   5. Therefore, you'll have to accordingly adjust the "Water Collection Rate" for the selected population of City & Town so that they don't run out of water.
  //   7. This with enable to effectively understand the necessity of water for the District and Analyse the consumption and avail the right input rates for the right population. 
  //   a. You can adjust the population by adding/subtracting using the "Population Rate" to choose the rate & the right Switch to execute the process.
  //   THE TOWN
  //   b. You can also change the "Rate" of the Population Adder/Subtractor and the "Water Collection Rate" at any point of time to match and analyze at different circumstances.
  //   6. If there is Insufficient Water for the Town/City, the water supply for both will be halted so that the Water Reservoir can Analyze the Supply and Adjust the "Water Collection Rate" to meet the District's Need.
endmodule

module _6_Bit_FlipFlop_D (
  input  [5:0] _6_Bit_Input,
  input  Load__1_updates_the_memory,
  input  Reset,
  output [5:0] _6_Bit_Stored_Output
);

  wire clock_1_out;

  Clock clock_1 (.out(clock_1_out));
  D_Flip_Flop d_ff_1 (
    .clk(clock_1_out), .D(_6_Bit_Input[0]), .Q(_6_Bit_Stored_Output[0]), .en(Load__1_updates_the_memory),
    .reset(Reset));  // open: Qn, preset
  D_Flip_Flop d_ff_2 (
    .clk(clock_1_out), .D(_6_Bit_Input[1]), .Q(_6_Bit_Stored_Output[1]), .en(Load__1_updates_the_memory),
    .reset(Reset));  // open: Qn, preset
  D_Flip_Flop d_ff_3 (
    .clk(clock_1_out), .D(_6_Bit_Input[2]), .Q(_6_Bit_Stored_Output[2]), .en(Load__1_updates_the_memory),
    .reset(Reset));  // open: Qn, preset
  D_Flip_Flop d_ff_4 (
    .clk(clock_1_out), .D(_6_Bit_Input[3]), .Q(_6_Bit_Stored_Output[3]), .en(Load__1_updates_the_memory),
    .reset(Reset));  // open: Qn, preset
  D_Flip_Flop d_ff_5 (
    .clk(clock_1_out), .D(_6_Bit_Input[4]), .Q(_6_Bit_Stored_Output[4]), .en(Load__1_updates_the_memory),
    .reset(Reset));  // open: Qn, preset
  D_Flip_Flop d_ff_6 (
    .clk(clock_1_out), .D(_6_Bit_Input[5]), .Q(_6_Bit_Stored_Output[5]), .en(Load__1_updates_the_memory),
    .reset(Reset));  // open: Qn, preset
endmodule

module _6_bit_subtractor (
  input  [5:0] Bigger_Number,
  input  [5:0] Smaller_Number,
  output [5:0] Difference,
  output Overflow__1___if_Bigger___Smaller
);

  Subtractor #(.width(6)) subtractor_1 (
    .a(Bigger_Number), .b(Smaller_Number), .out(Difference), .bout(Overflow__1___if_Bigger___Smaller));  // open: bin
endmodule

module _5_bit_Divider__by_4 (
  input  [4:0] Input,
  output [3:0] Ans__Input___4__rounded
);

  wire adder_1_cout;
  wire [0:0] and_1_out;

  and and_1 (and_1_out[0], Input[0], Input[1]);
  Adder #(.width(4)) adder_1 (
    .a({1'b0, Input[4:2]}), .b({3'b000, and_1_out[0]}), .out(Ans__Input___4__rounded), .cout(adder_1_cout));  // open: cin
endmodule

module _6_bit_Adder (
  input  [5:0] Input1,
  input  [5:0] Input2,
  output [5:0] Sum,
  output Overflow
);

  Adder #(.width(6)) adder_1 (.a(Input1), .b(Input2), .out(Sum), .cout(Overflow));  // open: cin
endmodule

module _4_bit_Multiplier__by_3 (
  input  [3:0] Input,
  output [5:0] Ans__Input_x_3
);

  _6_bit_Adder u_6_bit_adder_1 (
    .Input1({2'b00, Input}), .Input2({1'b0, Input, 1'b0}), .Sum(Ans__Input_x_3));  // open: Overflow
endmodule

module _4_bit_FlipFlop_D (
  input  [3:0] _4_Bit_Input,
  input  Load__1_updates_the_memory,
  input  Reset,
  output [3:0] _4_Bit_Stored_Output
);

  wire clock_1_out;

  Clock #(.highDuration(8), .lowDuration(8)) clock_1 (.out(clock_1_out));
  D_Flip_Flop d_ff_1 (
    .clk(clock_1_out), .D(_4_Bit_Input[3]), .Q(_4_Bit_Stored_Output[3]), .en(Load__1_updates_the_memory),
    .reset(Reset));  // open: Qn, preset
  D_Flip_Flop d_ff_2 (
    .clk(clock_1_out), .D(_4_Bit_Input[2]), .Q(_4_Bit_Stored_Output[2]), .en(Load__1_updates_the_memory),
    .reset(Reset));  // open: Qn, preset
  D_Flip_Flop d_ff_3 (
    .clk(clock_1_out), .D(_4_Bit_Input[1]), .Q(_4_Bit_Stored_Output[1]), .en(Load__1_updates_the_memory),
    .reset(Reset));  // open: Qn, preset
  D_Flip_Flop d_ff_4 (
    .clk(clock_1_out), .D(_4_Bit_Input[0]), .Q(_4_Bit_Stored_Output[0]), .en(Load__1_updates_the_memory),
    .reset(Reset));  // open: Qn, preset
endmodule

module _3_bit_FlipFlop__D (
  input  [2:0] _3_Bit_Input,
  input  Load__1_updates_the_memory,
  input  Reset,
  output [2:0] _3_Bit_Stored_Output
);

  wire clock_1_out;

  Clock #(.highDuration(8), .lowDuration(8)) clock_1 (.out(clock_1_out));
  D_Flip_Flop d_ff_1 (
    .clk(clock_1_out), .D(_3_Bit_Input[2]), .Q(_3_Bit_Stored_Output[2]), .en(Load__1_updates_the_memory),
    .reset(Reset));  // open: Qn, preset
  D_Flip_Flop d_ff_2 (
    .clk(clock_1_out), .D(_3_Bit_Input[1]), .Q(_3_Bit_Stored_Output[1]), .en(Load__1_updates_the_memory),
    .reset(Reset));  // open: Qn, preset
  D_Flip_Flop d_ff_3 (
    .clk(clock_1_out), .D(_3_Bit_Input[0]), .Q(_3_Bit_Stored_Output[0]), .en(Load__1_updates_the_memory),
    .reset(Reset));  // open: Qn, preset
endmodule

module _5_bit_Flipflop (
  input  [4:0] _5_Bit_Input,
  input  Load__1_updates_the_memory,
  output [4:0] _5_Bit_Stored_Output
);

  wire clock_1_out;

  Clock #(.highDuration(30), .lowDuration(30)) clock_1 (.out(clock_1_out));
  D_Flip_Flop d_ff_1 (
    .clk(clock_1_out), .D(_5_Bit_Input[4]), .Q(_5_Bit_Stored_Output[4]), .en(Load__1_updates_the_memory));  // open: Qn, preset, reset
  D_Flip_Flop d_ff_2 (
    .clk(clock_1_out), .D(_5_Bit_Input[3]), .Q(_5_Bit_Stored_Output[3]), .en(Load__1_updates_the_memory));  // open: Qn, preset, reset
  D_Flip_Flop d_ff_3 (
    .clk(clock_1_out), .D(_5_Bit_Input[2]), .Q(_5_Bit_Stored_Output[2]), .en(Load__1_updates_the_memory));  // open: Qn, preset, reset
  D_Flip_Flop d_ff_4 (
    .clk(clock_1_out), .D(_5_Bit_Input[1]), .Q(_5_Bit_Stored_Output[1]), .en(Load__1_updates_the_memory));  // open: Qn, preset, reset
  D_Flip_Flop d_ff_5 (
    .clk(clock_1_out), .D(_5_Bit_Input[0]), .Q(_5_Bit_Stored_Output[0]), .en(Load__1_updates_the_memory));  // open: Qn, preset, reset
endmodule

module Display___6_bit (
  input  [5:0] Input,
  output _100,
  output _75,
  output _50,
  output _25,
  output _10
);

  wire _6_plus_out, _16_plus_out, _31_plus_out, _47_plus_out, and_1_out;

  and _63 (_100, Input[5], Input[0], Input[1], Input[2], Input[3], Input[4]);
  and _47_plus (_47_plus_out, Input[5], Input[0], Input[1], Input[2], Input[3]);
  and _31_plus (_31_plus_out, Input[1], Input[2], Input[0], Input[3], Input[4]);
  and _16_plus (_16_plus_out, Input[4], Input[4]);
  and _6_plus (_6_plus_out, Input[1], Input[2]);
  and and_1 (and_1_out, Input[4], Input[5]);
  or or_1 (_75, and_1_out, _47_plus_out);
  or or_2 (_50, Input[5], _31_plus_out);
  or or_3 (_25, Input[5], _16_plus_out);
  or or_4 (_10, Input[3], Input[4], Input[5], _6_plus_out);
endmodule

module Display___4_bit (
  input  [3:0] Input,
  output _100,
  output _75,
  output _50,
  output _25
);

  wire _4_plus_out, _7_plus_out, _11_plus_out, and_1_out;

  and _15 (_100, Input[0], Input[1], Input[2], Input[3]);
  and _11_plus (_11_plus_out, Input[0], Input[1], Input[3]);
  and _7_plus (_7_plus_out, Input[2], Input[1], Input[0]);
  and _4_plus (_4_plus_out, Input[2], Input[2]);
  and and_1 (and_1_out, Input[2], Input[3]);
  or or_1 (_75, and_1_out, _11_plus_out);
  or or_2 (_50, Input[3], _7_plus_out);
  or or_3 (_25, Input[3], _4_plus_out);
endmodule

module Display___3_bit (
  input  [2:0] Input,
  output _100,
  output _60,
  output _30
);

  and _7 (_100, Input[0], Input[1], Input[2]);
  or or_1 (_30, Input[2], Input[1]);

  assign _60 = Input[2];
endmodule

module _4_bit_Adder (
  input  [3:0] Input1,
  input  [3:0] Input2,
  output [3:0] Sum,
  output Overflow
);

  Adder #(.width(4)) adder_1 (.a(Input1), .b(Input2), .out(Sum), .cout(Overflow));  // open: cin
endmodule

module _3_bit_Adder (
  input  [2:0] Input1,
  input  [2:0] Input2,
  output [2:0] Sum,
  output Overflow
);

  Adder #(.width(3)) adder_1 (.a(Input1), .b(Input2), .out(Sum), .cout(Overflow));  // open: cin
endmodule

module _4_bit_Subtractor (
  input  [3:0] Bigger_Number,
  input  [3:0] Smaller_Number,
  output [3:0] Difference,
  output Overflow__1___if_Bigger___Smaller
);

  Subtractor #(.width(4)) subtractor_1 (
    .a(Bigger_Number), .b(Smaller_Number), .out(Difference), .bout(Overflow__1___if_Bigger___Smaller));  // open: bin
endmodule

module _3_bit_Subtractor (
  input  [2:0] Bigger_Number,
  input  [2:0] Smaller_Number,
  output [2:0] Difference,
  output Overflow__1___if_Bigger___Smaller
);

  Subtractor #(.width(3)) subtractor_1 (
    .a(Bigger_Number), .b(Smaller_Number), .out(Difference), .bout(Overflow__1___if_Bigger___Smaller));  // open: bin
endmodule

module _3_4_convertor___3_bit (
  input  [2:0] Input,
  output [2:0] Input_3_4
);

  wire [3:3] n5_bit_divider_by_4_1_ans__input___4__rounded;
  wire [5:0] n4_bit_multiplier_by_3_1_ans__input_x_3;

  _4_bit_Multiplier__by_3 u_4_bit_multiplier_by_3_1 (
    .Input({1'b0, Input}), .Ans__Input_x_3(n4_bit_multiplier_by_3_1_ans__input_x_3));
  _5_bit_Divider__by_4 u_5_bit_divider_by_4_1 (
    .Input(n4_bit_multiplier_by_3_1_ans__input_x_3[4:0]),
    .Ans__Input___4__rounded({n5_bit_divider_by_4_1_ans__input___4__rounded[3], Input_3_4}));
endmodule

module _3_4_convertor___4_bit (
  input  [3:0] Input,
  output [3:0] Input_3_4
);

  wire [4:4] n6_bit_divider_by_4_1_ans__input___4__rounded;
  wire [5:0] n4_bit_multiplier_by_3_1_ans__input_x_3;

  _4_bit_Multiplier__by_3 u_4_bit_multiplier_by_3_1 (
    .Input(Input), .Ans__Input_x_3(n4_bit_multiplier_by_3_1_ans__input_x_3));
  _6_bit_Divider__by_4 u_6_bit_divider_by_4_1 (
    .Input(n4_bit_multiplier_by_3_1_ans__input_x_3),
    .Ans__Input___4__rounded({n6_bit_divider_by_4_1_ans__input___4__rounded[4], Input_3_4}));
endmodule

module _6_bit_Divider__by_4 (
  input  [5:0] Input,
  output [4:0] Ans__Input___4__rounded
);

  wire adder_1_cout;
  wire [0:0] and_1_out;

  and and_1 (and_1_out[0], Input[0], Input[1]);
  Adder #(.width(5)) adder_1 (
    .a({1'b0, Input[5:2]}), .b({4'b0000, and_1_out[0]}), .out(Ans__Input___4__rounded), .cout(adder_1_cout));  // open: cin
endmodule

module _3_4_convertor___5_bit (
  input  [4:0] Input,
  output [4:0] Input_3_4
);

  wire [3:0] n5_bit_divider_by_4_1_ans__input___4__rounded;
  wire [5:5] n4_bit_multiplier_by_3_1_ans__input_x_3;

  _5_bit_Divider__by_4 u_5_bit_divider_by_4_1 (
    .Input(Input), .Ans__Input___4__rounded(n5_bit_divider_by_4_1_ans__input___4__rounded));
  _4_bit_Multiplier__by_3 u_4_bit_multiplier_by_3_1 (
    .Input(n5_bit_divider_by_4_1_ans__input___4__rounded),
    .Ans__Input_x_3({n4_bit_multiplier_by_3_1_ans__input_x_3[5], Input_3_4}));
endmodule
