// Logisim project S1-T12_Simplified_v3.circ as structural Verilog: 3 circuits, main circuit main
module main (
  input  A1,
  input  A0,
  input  Load,
  input  A2,
  input  A1_2,
  input  A0_2
);

  wire and_2_out, and_3_out, and_4_out, Clock_out, Reset_out, Set_Water_out;
  wire [1:0] xor_1_out;
  wire [2:0] A0_q, adder_1_out, adder_2_out, and_5_out, not_3_out;
  wire [2:2] adder_2_cout;

  Clock Clock (.out(Clock_out));
  Button Reset (.out(Reset_out));
  Button Set_Water (.out(Set_Water_out));
  and and_1 (xor_1_out[1], A1, A0);
  xor xor_1 (xor_1_out[0], A1, A0);
  and and_2 (and_2_out, A2, Set_Water_out);
  and and_3 (and_3_out, A1_2, Set_Water_out);
  and and_4 (and_4_out, A0_2, Set_Water_out);
  not not_1 (not_3_out[2], 1'b0);
  not not_2 (not_3_out[1], A1);
  not not_3 (not_3_out[0], A0);
  Adder #(.width(3)) adder_1 (.a(not_3_out), .b({1'b0, xor_1_out}), .out(adder_1_out), .cin(1'b1));  // open: cout
  D_Flip_Flop u_A2 (
    .clk(Clock_out), .D(and_5_out[2]), .Q(A0_q[2]), .preset(and_2_out), .en(Load), .reset(Reset_out));  // open: Qn
  D_Flip_Flop u_A1 (
    .clk(Clock_out), .D(and_5_out[1]), .Q(A0_q[1]), .preset(and_3_out), .en(Load), .reset(Reset_out));  // open: Qn
  D_Flip_Flop u_A0 (
    .clk(Clock_out), .D(and_5_out[0]), .Q(A0_q[0]), .preset(and_4_out), .en(Load), .reset(Reset_out));  // open: Qn
  Adder #(.width(3)) adder_2 (.a(adder_1_out), .b(A0_q), .out(adder_2_out), .cin(1'b0), .cout(adder_2_cout[2]));
  assign and_5_out = {3{adder_2_cout[2]}} & adder_2_out;  // AND_Gate and_5, 3 bits wide

  // Notes on the sheet:
  //   Population
  //   -City+Sewage
  //   preset the water level, and with abutton, initate the same value in the flip-flop and then recursively subtract from the flipflop.
endmodule

module _3_bit_Display (
  input  A2,
  input  A1,
  input  A0,
  output _100,
  output _67,
  output _33
);

  wire and_1_out, and_2_out, not_1_out, not_2_out, not_3_out, xor_1_out;

  xor xor_1 (xor_1_out, A0, A1);
  not not_1 (not_1_out, A2);
  and and_1 (and_1_out, not_1_out, A1);
  not not_2 (not_2_out, A1);
  and and_2 (and_2_out, A2, not_2_out, not_3_out);
  not not_3 (not_3_out, A0);
  and and_3 (_100, A2, A1, A0);
  and and_4 (_67, A2, xor_1_out);
  or or_1 (_33, and_1_out, and_2_out);
endmodule

module Submain (
  input  A1,
  input  A0,
  output City_Underflow,
  output _0,
  output _14,
  output _28,
  output _43,
  output _57,
  output _72,
  output _86,
  output _100
);

  wire adder_1_cout, and_1_out, and_2_out, clock_1_out, Full_Water_out, not_3_out, xor_1_out;
  wire [1:0] not_2_out;
  wire [2:0] adder_1_out, d_ff_3_q;

  Clock clock_1 (.out(clock_1_out));
  Button Full_Water (.out(Full_Water_out));
  and and_1 (and_1_out, A1, A0);
  xor xor_1 (xor_1_out, A1, A0);
  not not_1 (not_2_out[1], and_1_out);
  not not_2 (not_2_out[0], xor_1_out);
  D_Flip_Flop d_ff_1 (
    .clk(clock_1_out), .D(adder_1_out[2]), .Q(d_ff_3_q[2]), .preset(Full_Water_out), .reset(and_2_out));  // open: Qn, en
  D_Flip_Flop d_ff_2 (
    .clk(clock_1_out), .D(adder_1_out[1]), .Q(d_ff_3_q[1]), .preset(Full_Water_out), .reset(and_2_out));  // open: Qn, en
  D_Flip_Flop d_ff_3 (
    .clk(clock_1_out), .D(adder_1_out[0]), .Q(d_ff_3_q[0]), .preset(Full_Water_out), .reset(and_2_out));  // open: Qn, en
  not not_3 (not_3_out, Full_Water_out);
  Adder #(.width(3)) adder_1 (.a({1'b1, not_2_out}), .b(d_ff_3_q), .out(adder_1_out), .cin(1'b1), .cout(adder_1_cout));
  not not_4 (City_Underflow, adder_1_cout);
  and and_2 (and_2_out, not_3_out, City_Underflow);
  Decoder #(.select(3)) decoder_1 (
    .out0(_0), .out1(_14), .out2(_28), .out3(_43), .out4(_57), .out5(_72), .out6(_86), .out7(_100),
    .sel(d_ff_3_q), .en(1'b1));

  // Notes on the sheet:
  //   Population
endmodule
